// Logisim project projet_Processeur.circ as structural Verilog: 48 circuits, main circuit main
module main (
  input  init,
  output [7:0] res,
  output erreur
);

  wire and_1_out, and_2_out, decodeur_1_jeq, decodeur_1_jmp, decodeur_1_jne, decodeur_1_stor, decodeur_1_we,
       not_1_out, or_1_out, or_2_out;
  wire [1:0] decodeur_1_instructionreg, decodeur_1_typeope;
  wire [2:0] decodeur_1_op, decodeur_1_rin1, decodeur_1_rin2, decodeur_1_rout;
  wire [7:0] addressingregisters_1_reg_in, bancregistre_1_memoire1, bancregistre_1_memoire2,
       bancregistre_1_memoire3, bancregistre_1_memoire4, bancregistre_1_memoire5, bancregistre_1_memoire6,
       bancregistre_1_memoire7, bancregistre_1_memoire8, decodeur_1_addr8_cnst8, multiplexer_1_out,
       multiplexer_2_out, ramdonnees_1_sortie;
  wire [23:0] chemindonnees_1_out_4;

  Clock infoClock ();  // open: out
  RAMdonnees ramdonnees_1 (
    .adresse(decodeur_1_addr8_cnst8), .WE(decodeur_1_stor), .entre(multiplexer_1_out),
    .sortie(ramdonnees_1_sortie));
  CheminDonnees chemindonnees_1 (
    .ADDR8(decodeur_1_addr8_cnst8), .JUMP(or_1_out), .init(init), .out_4(chemindonnees_1_out_4));
  or or_1 (or_1_out, and_1_out, or_2_out);
  or or_2 (or_2_out, and_2_out, decodeur_1_jmp);
  decodeur decodeur_1 (
    .instruction(chemindonnees_1_out_4), .typeOpe(decodeur_1_typeope), .OP(decodeur_1_op),
    .Rin1(decodeur_1_rin1), .Rin2(decodeur_1_rin2), .Rout(decodeur_1_rout),
    .Addr8_Cnst8(decodeur_1_addr8_cnst8), .instructionReg(decodeur_1_instructionreg), .WE(decodeur_1_we),
    .Stor(decodeur_1_stor), .Jmp(decodeur_1_jmp), .Jne(decodeur_1_jne), .Jeq(decodeur_1_jeq));  // open: Page
  and and_1 (and_1_out, bancregistre_1_memoire8[0], decodeur_1_jeq);
  and and_2 (and_2_out, not_1_out, decodeur_1_jne);
  addressingRegisters addressingregisters_1 (
    .ALU(res), .RAM(ramdonnees_1_sortie), .CNST8(decodeur_1_addr8_cnst8),
    .instruction(decodeur_1_instructionreg), .REG_IN(addressingregisters_1_reg_in));
  not not_1 (not_1_out, bancregistre_1_memoire8[0]);
  BancRegistre bancregistre_1 (
    .Value(addressingregisters_1_reg_in), .WE(decodeur_1_we), .right(decodeur_1_rout),
    .memoire1(bancregistre_1_memoire1), .memoire2(bancregistre_1_memoire2),
    .memoire3(bancregistre_1_memoire3), .memoire4(bancregistre_1_memoire4),
    .memoire5(bancregistre_1_memoire5), .memoire6(bancregistre_1_memoire6),
    .memoire7(bancregistre_1_memoire7), .memoire8(bancregistre_1_memoire8));
  // NoConnect on bancregistre_1_memoire8[5]
  // NoConnect on bancregistre_1_memoire8[4]
  // NoConnect on bancregistre_1_memoire8[3]
  // NoConnect on bancregistre_1_memoire8[2]
  // NoConnect on bancregistre_1_memoire8[7]
  // NoConnect on bancregistre_1_memoire8[6]
  // NoConnect on bancregistre_1_memoire8[1]
  Multiplexer #(.select(3), .width(8)) multiplexer_1 (
    .in0(bancregistre_1_memoire1), .in1(bancregistre_1_memoire2), .in2(bancregistre_1_memoire3),
    .in3(bancregistre_1_memoire4), .in4(bancregistre_1_memoire5), .in5(bancregistre_1_memoire6),
    .in6(bancregistre_1_memoire7), .in7(bancregistre_1_memoire8), .out(multiplexer_1_out),
    .sel(decodeur_1_rin1));
  Multiplexer #(.select(3), .width(8)) multiplexer_2 (
    .in0(bancregistre_1_memoire1), .in1(bancregistre_1_memoire2), .in2(bancregistre_1_memoire3),
    .in3(bancregistre_1_memoire4), .in4(bancregistre_1_memoire5), .in5(bancregistre_1_memoire6),
    .in6(bancregistre_1_memoire7), .in7(bancregistre_1_memoire8), .out(multiplexer_2_out),
    .sel(decodeur_1_rin2));
  UAL ual_1 (
    .A(multiplexer_1_out), .B(multiplexer_2_out), .typeOpe(decodeur_1_typeope), .ope(decodeur_1_op),
    .res(res), .erreur(erreur));

  // Notes on the sheet:
  //   init: initial=0x1
endmodule

module add1bit (
  input  A,
  input  B,
  input  R,
  output res,
  output res_R
);

  wire and_1_out, and_2_out, and_3_out, or_1_out, xor_1_out;

  xor xor_1 (xor_1_out, A, B);
  and and_1 (and_1_out, A, B);
  and and_2 (and_2_out, R, A);
  and and_3 (and_3_out, R, B);
  xor xor_2 (res, xor_1_out, R);
  or or_1 (or_1_out, and_2_out, and_3_out);
  or or_2 (res_R, and_1_out, or_1_out);
endmodule

module add (
  input  [7:0] A,
  input  [7:0] B,
  output [7:0] res,
  output overflow
);

  wire add1bit_1_res_r, add1bit_2_res_r, add1bit_3_res_r, add1bit_4_res_r, add1bit_5_res_r, add1bit_6_res_r,
       add1bit_7_res_r;

  add1bit add1bit_1 (.A(A[0]), .B(B[0]), .R(1'b0), .res(res[0]), .res_R(add1bit_1_res_r));
  add1bit add1bit_2 (.A(A[1]), .B(B[1]), .R(add1bit_1_res_r), .res(res[1]), .res_R(add1bit_2_res_r));
  add1bit add1bit_3 (.A(A[2]), .B(B[2]), .R(add1bit_2_res_r), .res(res[2]), .res_R(add1bit_3_res_r));
  add1bit add1bit_4 (.A(A[3]), .B(B[3]), .R(add1bit_3_res_r), .res(res[3]), .res_R(add1bit_4_res_r));
  add1bit add1bit_5 (.A(A[4]), .B(B[4]), .R(add1bit_4_res_r), .res(res[4]), .res_R(add1bit_5_res_r));
  add1bit add1bit_6 (.A(A[5]), .B(B[5]), .R(add1bit_5_res_r), .res(res[5]), .res_R(add1bit_6_res_r));
  add1bit add1bit_7 (.A(A[6]), .B(B[6]), .R(add1bit_6_res_r), .res(res[6]), .res_R(add1bit_7_res_r));
  add1bit add1bit_8 (.A(A[7]), .B(B[7]), .R(add1bit_7_res_r), .res(res[7]), .res_R(overflow));
endmodule

module sub (
  input  [7:0] A,
  input  [7:0] B,
  output [7:0] res,
  output erreur
);

  wire add_1_overflow, add_2_overflow;
  wire [7:0] add_1_res, not_1_out;

  assign not_1_out = ~B;  // NOT_Gate not_1, 8 bits wide
  add add_1 (.A(not_1_out), .B(8'h1), .res(add_1_res), .overflow(add_1_overflow));
  // NoConnect on add_1_overflow
  add add_2 (.A(A), .B(add_1_res), .res(res), .overflow(add_2_overflow));
  // NoConnect on add_2_overflow

  assign erreur = B[7];
endmodule

module MAX (
  input  [7:0] A,
  input  [7:0] B,
  output [7:0] res
);

  wire inf_1_res;

  inf inf_1 (.A(A), .B(B), .res(inf_1_res));
  Multiplexer #(.width(8)) multiplexer_1 (.in0(A), .in1(B), .out(res), .sel(inf_1_res));
endmodule

module MIN (
  input  [7:0] A,
  input  [7:0] B,
  output [7:0] res
);

  wire sup_1_res;

  sup sup_1 (.A(A), .B(B), .res(sup_1_res));
  Multiplexer #(.width(8)) multiplexer_1 (.in0(A), .in1(B), .out(res), .sel(sup_1_res));
endmodule

module INC (
  input  [7:0] A,
  output [7:0] res,
  output overflow
);

  add add_1 (.A(A), .B(8'h1), .res(res), .overflow(overflow));
endmodule

module DEC (
  input  [7:0] A,
  output [7:0] res,
  output erreur
);

  sub sub_1 (.A(A), .B(8'h1), .res(res), .erreur(erreur));
endmodule

module Absolute (
  input  [7:0] A,
  output [7:0] res
);


  assign res = {1'b0, A[6:0]};
endmodule

module NEG (
  input  [7:0] A,
  output [7:0] res
);


  assign res = {1'b1, A[6:0]};
endmodule

module and8bit (
  input  [7:0] A,
  input  [7:0] B,
  output [7:0] res
);

  assign res = A & B;  // AND_Gate and_1, 8 bits wide
endmodule

module or8bit (
  input  [7:0] A,
  input  [7:0] B,
  output [7:0] res
);

  assign res = A | B;  // OR_Gate or_1, 8 bits wide
endmodule

module xor8bit (
  input  [7:0] A,
  input  [7:0] B,
  output [7:0] res
);

  assign res = A ^ B;  // XOR_Gate xor_1, 8 bits wide
endmodule

module nand8bit (
  input  [7:0] A,
  input  [7:0] B,
  output [7:0] res
);

  wire [7:0] and8bit_1_res;

  assign res = ~and8bit_1_res;  // NOT_Gate not_1, 8 bits wide
  and8bit and8bit_1 (.A(A), .B(B), .res(and8bit_1_res));
endmodule

module nor8bit (
  input  [7:0] A,
  input  [7:0] B,
  output [7:0] res
);

  wire [7:0] or8bit_1_res;

  assign res = ~or8bit_1_res;  // NOT_Gate not_1, 8 bits wide
  or8bit or8bit_1 (.A(A), .B(B), .res(or8bit_1_res));
endmodule

module xnor8bit (
  input  [7:0] A,
  input  [7:0] B,
  output [7:0] res
);

  wire [7:0] xor8bit_1_res;

  assign res = ~xor8bit_1_res;  // NOT_Gate not_1, 8 bits wide
  xor8bit xor8bit_1 (.A(A), .B(B), .res(xor8bit_1_res));
endmodule

module not8bit (
  input  [7:0] A,
  output [7:0] res
);

  assign res = ~A;  // NOT_Gate not_1, 8 bits wide
endmodule

module LSL (
  input  [7:0] A,
  output [7:0] res
);


  assign res = {A[6:0], 1'b0};
endmodule

module LSR (
  input  [7:0] A,
  output [7:0] res
);


  assign res = {1'b0, A[7:1]};
endmodule

module ASL (
  input  [7:0] A,
  output [7:0] res
);


  assign res = {A[7], A[5:0], 1'b0};
endmodule

module ASR (
  input  [7:0] A,
  output [7:0] res
);


  assign res = {{2{A[7]}}, A[6:2], A[0]};
endmodule

module rol8bit (
  input  [7:0] A,
  output [7:0] res
);


  assign res = {A[6:0], A[7]};
endmodule

module ror8bit (
  input  [7:0] A,
  output [7:0] res
);


  assign res = {A[0], A[7:1]};
endmodule

module Equal (
  input  [7:0] A,
  input  [7:0] B,
  output res
);

  wire [7:0] not_1_out, xor_1_out;

  assign xor_1_out = A ^ B;  // XOR_Gate xor_1, 8 bits wide
  assign not_1_out = ~xor_1_out;  // NOT_Gate not_1, 8 bits wide
  and and_1 (res, not_1_out[0], not_1_out[1], not_1_out[2], not_1_out[3], not_1_out[4], not_1_out[5], not_1_out[6], not_1_out[7]);
endmodule

module diff (
  input  [7:0] A,
  input  [7:0] B,
  output res
);

  wire equal_1_res;

  Equal equal_1 (.A(A), .B(B), .res(equal_1_res));
  not not_1 (res, equal_1_res);
endmodule

module inf1bit (
  input  suivant,
  input  A,
  input  B,
  output res,
  output \continue 
);

  wire and_1_out, not_1_out, not_2_out, xor_1_out;

  not not_1 (not_1_out, A);
  and and_1 (and_1_out, not_1_out, B);
  xor xor_1 (xor_1_out, A, B);
  not not_2 (not_2_out, xor_1_out);
  and and_2 (res, and_1_out, suivant);
  and and_3 (\continue , suivant, not_2_out);
endmodule

module inf (
  input  [7:0] A,
  input  [7:0] B,
  output res
);

  wire inf1bit_1_continue, inf1bit_1_res, inf1bit_2_continue, inf1bit_2_res, inf1bit_3_continue,
       inf1bit_3_res, inf1bit_4_continue, inf1bit_4_res, inf1bit_5_continue, inf1bit_5_res,
       inf1bit_6_continue, inf1bit_6_res, inf1bit_7_continue, inf1bit_7_res, inf1bit_8_continue,
       inf1bit_8_res;

  inf1bit inf1bit_1 (.suivant(1'b1), .A(A[7]), .B(B[7]), .res(inf1bit_1_res), .\continue (inf1bit_1_continue));
  inf1bit inf1bit_2 (
    .suivant(inf1bit_1_continue), .A(A[6]), .B(B[6]), .res(inf1bit_2_res), .\continue (inf1bit_2_continue));
  inf1bit inf1bit_3 (
    .suivant(inf1bit_2_continue), .A(A[5]), .B(B[5]), .res(inf1bit_3_res), .\continue (inf1bit_3_continue));
  inf1bit inf1bit_4 (
    .suivant(inf1bit_3_continue), .A(A[4]), .B(B[4]), .res(inf1bit_4_res), .\continue (inf1bit_4_continue));
  inf1bit inf1bit_5 (
    .suivant(inf1bit_4_continue), .A(A[3]), .B(B[3]), .res(inf1bit_5_res), .\continue (inf1bit_5_continue));
  inf1bit inf1bit_6 (
    .suivant(inf1bit_5_continue), .A(A[2]), .B(B[2]), .res(inf1bit_6_res), .\continue (inf1bit_6_continue));
  inf1bit inf1bit_7 (
    .suivant(inf1bit_6_continue), .A(A[1]), .B(B[1]), .res(inf1bit_7_res), .\continue (inf1bit_7_continue));
  inf1bit inf1bit_8 (
    .suivant(inf1bit_7_continue), .A(A[0]), .B(B[0]), .res(inf1bit_8_res), .\continue (inf1bit_8_continue));
  // NoConnect on inf1bit_8_continue
  or or_1 (res, inf1bit_1_res, inf1bit_2_res, inf1bit_3_res, inf1bit_4_res, inf1bit_5_res, inf1bit_6_res, inf1bit_7_res, inf1bit_8_res);
endmodule

module infEqual (
  input  [7:0] A,
  input  [7:0] B,
  output res
);

  wire equal_1_res, inf_1_res;

  inf inf_1 (.A(A), .B(B), .res(inf_1_res));
  Equal equal_1 (.A(A), .B(B), .res(equal_1_res));
  or or_1 (res, inf_1_res, equal_1_res);
endmodule

module sup (
  input  [7:0] A,
  input  [7:0] B,
  output res
);

  wire equal_1_res, inf_1_res, not_1_out, not_2_out;

  not not_1 (not_1_out, inf_1_res);
  inf inf_1 (.A(A), .B(B), .res(inf_1_res));
  not not_2 (not_2_out, equal_1_res);
  Equal equal_1 (.A(A), .B(B), .res(equal_1_res));
  and and_1 (res, not_1_out, not_2_out);
endmodule

module supEqual (
  input  [7:0] A,
  input  [7:0] B,
  output res
);

  wire inf_1_res;

  not not_1 (res, inf_1_res);
  inf inf_1 (.A(A), .B(B), .res(inf_1_res));
endmodule

module notEqual (
  input  [7:0] A,
  input  [7:0] B,
  output res
);

  wire equal_1_res;

  Equal equal_1 (.A(A), .B(B), .res(equal_1_res));
  not not_1 (res, equal_1_res);
endmodule

module BlocArithmetiques (
  input  [7:0] A,
  input  [7:0] B,
  input  [2:0] ope,
  output [7:0] res,
  output erreur
);

  wire add_1_overflow, dec_1_erreur, inc_1_overflow, sub_1_erreur;
  wire [7:0] absolute_1_res, add_1_res, dec_1_res, inc_1_res, max_1_res, min_1_res, neg_1_res, sub_1_res;

  add add_1 (.A(A), .B(B), .res(add_1_res), .overflow(add_1_overflow));
  sub sub_1 (.A(A), .B(B), .res(sub_1_res), .erreur(sub_1_erreur));
  MIN min_1 (.A(A), .B(B), .res(min_1_res));
  MAX max_1 (.A(A), .B(B), .res(max_1_res));
  INC inc_1 (.A(A), .res(inc_1_res), .overflow(inc_1_overflow));
  DEC dec_1 (.A(A), .res(dec_1_res), .erreur(dec_1_erreur));
  NEG neg_1 (.A(A), .res(neg_1_res));
  Absolute absolute_1 (.A(A), .res(absolute_1_res));
  Multiplexer #(.select(3), .width(8)) multiplexer_1 (
    .in0(add_1_res), .in1(sub_1_res), .in2(min_1_res), .in3(max_1_res), .in4(inc_1_res), .in5(dec_1_res),
    .in6(neg_1_res), .in7(absolute_1_res), .out(res), .sel(ope));
  Multiplexer #(.select(3)) multiplexer_2 (
    .in0(add_1_overflow), .in1(sub_1_erreur), .in2(1'b0), .in3(1'b0), .in4(inc_1_overflow),
    .in5(dec_1_erreur), .in6(1'b0), .in7(1'b0), .out(erreur), .sel(ope));
endmodule

module BlocLogiques2Reg (
  input  [7:0] A,
  input  [7:0] B,
  input  [2:0] ope,
  output [7:0] res
);

  wire [7:0] and8bit_1_res, nand8bit_1_res, nor8bit_1_res, or8bit_1_res, xnor8bit_1_res, xor8bit_1_res;

  and8bit and8bit_1 (.A(A), .B(B), .res(and8bit_1_res));
  or8bit or8bit_1 (.A(A), .B(B), .res(or8bit_1_res));
  xor8bit xor8bit_1 (.A(A), .B(B), .res(xor8bit_1_res));
  nand8bit nand8bit_1 (.A(A), .B(B), .res(nand8bit_1_res));
  nor8bit nor8bit_1 (.A(A), .B(B), .res(nor8bit_1_res));
  xnor8bit xnor8bit_1 (.A(A), .B(B), .res(xnor8bit_1_res));
  Multiplexer #(.select(3), .width(8)) multiplexer_1 (
    .in0(and8bit_1_res), .in1(or8bit_1_res), .in2(xor8bit_1_res), .in3(nand8bit_1_res), .in4(nor8bit_1_res),
    .in5(xnor8bit_1_res), .in6({8{1'b0}}), .in7({8{1'b0}}), .out(res), .sel(ope));
endmodule

module BlocLogiques1Reg (
  input  [7:0] A,
  input  [2:0] ope,
  output [7:0] res
);

  wire [7:0] asl_1_res, asr_1_res, lsl_1_res, lsr_1_res, not8bit_1_res, rol8bit_1_res, ror8bit_1_res;

  not8bit not8bit_1 (.A(A), .res(not8bit_1_res));
  LSL lsl_1 (.A(A), .res(lsl_1_res));
  LSR lsr_1 (.A(A), .res(lsr_1_res));
  ASR asr_1 (.A(A), .res(asr_1_res));
  rol8bit rol8bit_1 (.A(A), .res(rol8bit_1_res));
  ror8bit ror8bit_1 (.A(A), .res(ror8bit_1_res));
  ASL asl_1 (.A(A), .res(asl_1_res));
  Multiplexer #(.select(3), .width(8)) multiplexer_1 (
    .in0(not8bit_1_res), .in1(lsl_1_res), .in2(lsr_1_res), .in3(asr_1_res), .in4(rol8bit_1_res),
    .in5(ror8bit_1_res), .in6(asl_1_res), .in7({8{1'b0}}), .out(res), .sel(ope));
endmodule

module BlocComparaisons (
  input  [7:0] A,
  input  [7:0] B,
  input  [2:0] ope,
  output res
);

  wire equal_1_res, inf_1_res, infequal_1_res, notequal_1_res, sup_1_res, supequal_1_res;

  inf inf_1 (.A(A), .B(B), .res(inf_1_res));
  infEqual infequal_1 (.A(A), .B(B), .res(infequal_1_res));
  Equal equal_1 (.A(A), .B(B), .res(equal_1_res));
  supEqual supequal_1 (.A(A), .B(B), .res(supequal_1_res));
  sup sup_1 (.A(A), .B(B), .res(sup_1_res));
  notEqual notequal_1 (.A(A), .B(B), .res(notequal_1_res));
  Multiplexer #(.select(3)) multiplexer_1 (
    .in0(1'b0), .in1(inf_1_res), .in2(infequal_1_res), .in3(equal_1_res), .in4(supequal_1_res),
    .in5(sup_1_res), .in6(notequal_1_res), .in7(1'b0), .out(res), .sel(ope));
endmodule

module UAL (
  input  [7:0] A,
  input  [7:0] B,
  input  [1:0] typeOpe,
  input  [2:0] ope,
  output [7:0] res,
  output erreur
);

  wire blocarithmetiques_1_erreur, bloccomparaisons_1_res, or_1_out;
  wire [7:0] bit_extender_1_out, blocarithmetiques_1_res, bloclogiques1reg_1_res, bloclogiques2reg_1_res;

  BlocArithmetiques blocarithmetiques_1 (
    .A(A), .B(B), .ope(ope), .res(blocarithmetiques_1_res), .erreur(blocarithmetiques_1_erreur));
  BlocLogiques2Reg bloclogiques2reg_1 (.A(A), .B(B), .ope(ope), .res(bloclogiques2reg_1_res));
  BlocComparaisons bloccomparaisons_1 (.A(A), .B(B), .ope(ope), .res(bloccomparaisons_1_res));
  BlocLogiques1Reg bloclogiques1reg_1 (.A(A), .ope(ope), .res(bloclogiques1reg_1_res));
  assign bit_extender_1_out = {{7{1'b0}}, bloccomparaisons_1_res};  // Bit_Extender bit_extender_1
  Multiplexer #(.select(2), .width(8)) multiplexer_1 (
    .in0(bit_extender_1_out), .in1(bloclogiques1reg_1_res), .in2(bloclogiques2reg_1_res),
    .in3(blocarithmetiques_1_res), .out(res), .sel(typeOpe));
  Multiplexer multiplexer_2 (.in0(blocarithmetiques_1_erreur), .in1(1'b0), .out(erreur), .sel(or_1_out));
  or or_1 (or_1_out, typeOpe[0], typeOpe[1]);
endmodule

module Registre1bit (
  input  [7:0] D,
  input  WE,
  output [7:0] out_3
);

  wire clock_1_out, d_ff_1_q;
  wire [7:0] multiplexer_1_out;

  Clock clock_1 (.out(clock_1_out));
  Multiplexer #(.width(8)) multiplexer_1 (.in0(out_3), .in1(D), .out(multiplexer_1_out), .sel(WE));
  D_Flip_Flop d_ff_1 (.D(multiplexer_1_out[0]), .clk(clock_1_out), .Q(d_ff_1_q));  // open: Qn, preset, reset
  assign out_3 = {{7{1'b0}}, d_ff_1_q};  // Bit_Extender bit_extender_1
endmodule

module Registre8bit (
  input  [7:0] D,
  input  WE,
  output [7:0] out_3
);

  wire clock_1_out;
  wire [7:0] multiplexer_1_out;

  Multiplexer #(.width(8)) multiplexer_1 (.in0(out_3), .in1(D), .out(multiplexer_1_out), .sel(WE));
  Clock clock_1 (.out(clock_1_out));
  D_Flip_Flop d_ff_1 (.D(multiplexer_1_out[0]), .clk(clock_1_out), .Q(out_3[0]));  // open: Qn, preset, reset
  D_Flip_Flop d_ff_2 (.D(multiplexer_1_out[1]), .clk(clock_1_out), .Q(out_3[1]));  // open: Qn, preset, reset
  D_Flip_Flop d_ff_3 (.D(multiplexer_1_out[2]), .clk(clock_1_out), .Q(out_3[2]));  // open: Qn, preset, reset
  D_Flip_Flop d_ff_4 (.D(multiplexer_1_out[3]), .clk(clock_1_out), .Q(out_3[3]));  // open: Qn, preset, reset
  D_Flip_Flop d_ff_5 (.D(multiplexer_1_out[4]), .clk(clock_1_out), .Q(out_3[4]));  // open: Qn, preset, reset
  D_Flip_Flop d_ff_6 (.D(multiplexer_1_out[5]), .clk(clock_1_out), .Q(out_3[5]));  // open: Qn, preset, reset
  D_Flip_Flop d_ff_7 (.D(multiplexer_1_out[6]), .clk(clock_1_out), .Q(out_3[6]));  // open: Qn, preset, reset
  D_Flip_Flop d_ff_8 (.D(multiplexer_1_out[7]), .clk(clock_1_out), .Q(out_3[7]));  // open: Qn, preset, reset
endmodule

module BancRegistre (
  input  [7:0] Value,
  input  WE,
  input  [2:0] right,
  output [7:0] memoire1,
  output [7:0] memoire2,
  output [7:0] memoire3,
  output [7:0] memoire4,
  output [7:0] memoire5,
  output [7:0] memoire6,
  output [7:0] memoire7,
  output [7:0] memoire8
);

  wire demultiplexer_1_out0, demultiplexer_1_out1, demultiplexer_1_out2, demultiplexer_1_out3,
       demultiplexer_1_out4, demultiplexer_1_out5, demultiplexer_1_out6, demultiplexer_1_out7;

  Demultiplexer #(.select(3)) demultiplexer_1 (
    .out0(demultiplexer_1_out0), .out1(demultiplexer_1_out1), .out2(demultiplexer_1_out2),
    .out3(demultiplexer_1_out3), .out4(demultiplexer_1_out4), .out5(demultiplexer_1_out5),
    .out6(demultiplexer_1_out6), .out7(demultiplexer_1_out7), .in(WE), .sel(right));
  Registre8bit registre8bit_1 (.D(Value), .WE(demultiplexer_1_out0), .out_3(memoire1));
  Registre8bit registre8bit_2 (.D(Value), .WE(demultiplexer_1_out1), .out_3(memoire2));
  Registre8bit registre8bit_3 (.D(Value), .WE(demultiplexer_1_out2), .out_3(memoire3));
  Registre8bit registre8bit_4 (.D(Value), .WE(demultiplexer_1_out3), .out_3(memoire4));
  Registre8bit registre8bit_5 (.D(Value), .WE(demultiplexer_1_out4), .out_3(memoire5));
  Registre8bit registre8bit_6 (.D(Value), .WE(demultiplexer_1_out5), .out_3(memoire6));
  Registre8bit registre8bit_7 (.D(Value), .WE(demultiplexer_1_out6), .out_3(memoire7));
  Registre1bit registre1bit_1 (.D(Value), .WE(demultiplexer_1_out7), .out_3(memoire8));
endmodule

module decodeur (
  input  [23:0] instruction,
  output [1:0] typeOpe,
  output [2:0] OP,
  output [2:0] Rin1,
  output [2:0] Rin2,
  output [2:0] Rout,
  output [7:0] Addr8_Cnst8,
  output [1:0] instructionReg,
  output WE,
  output Stor,
  output Page,
  output Jmp,
  output Jne,
  output Jeq
);

  wire clock_1_out, comparator_1_eq, instructionorual_1_cnst, instructionorual_1_load, or_1_out;
  wire [3:1] register_1_q_3;
  wire [3:3] register_1_q, register_1_q_2;

  Register #(.width(24)) register_1 (
    .D(instruction), .clk(clock_1_out),
    .Q({register_1_q_3, typeOpe, OP, register_1_q_2[3], Rin1, Addr8_Cnst8, register_1_q[3], Rout}));  // open: en, clr
  Clock clock_1 (.out(clock_1_out));
  // NoConnect on register_1_q_3[2]
  // NoConnect on register_1_q_3[3]
  Comparator #(.width(24)) comparator_1 (
    .a({register_1_q_3, typeOpe, OP, register_1_q_2[3], Rin1, Addr8_Cnst8, register_1_q[3], Rout}),
    .b({24{1'b0}}), .eq(comparator_1_eq));  // open: gt, lt
  InstructionOrUAL instructionorual_1 (
    .WE(register_1_q_3[1]), .right(OP), .Load(instructionorual_1_load), .Stor(Stor), .Page(Page),
    .Cnst(instructionorual_1_cnst), .Jmp(Jmp), .Jne(Jne), .Jeq(Jeq));
  or or_1 (or_1_out, comparator_1_eq, Jmp, Jne, Jeq, Stor, Page);
  not not_1 (WE, or_1_out);
  Priority_Encoder #(.select(2)) priority_encoder_1 (
    .in0(1'b1), .in1(instructionorual_1_load), .in2(instructionorual_1_cnst), .out(instructionReg));  // open: in3, gs, en_out, en_in

  assign Rin2 = Addr8_Cnst8[6:4];
endmodule

module InstructionOrUAL (
  input  WE,
  input  [2:0] right,
  output Load,
  output Stor,
  output Page,
  output Cnst,
  output Jmp,
  output Jne,
  output Jeq
);

  Demultiplexer #(.select(3)) demultiplexer_1 (
    .out1(Load), .out2(Stor), .out3(Page), .out4(Cnst), .out5(Jmp), .out6(Jne), .out7(Jeq), .in(WE),
    .sel(right));  // open: out0
endmodule

module RAMinstructions (
  input  [7:0] adresse,
  input  init,
  output [23:0] sortie
);

  wire clock_1_out;
  wire [23:0] ram_1_dout, undriven;

  // NoConnect on undriven
  Clock clock_1 (.out(clock_1_out));
  RAM #(.dataWidth(24)) ram_1 (
    .addr(adresse), .we(1'b0), .oe(1'b1), .clk(clock_1_out), .din(undriven), .dout(ram_1_dout));
  Multiplexer #(.width(24)) multiplexer_1 (.in0(ram_1_dout), .in1({24{1'b0}}), .out(sortie), .sel(init));
endmodule

module RAMdonnees (
  input  [7:0] adresse,
  input  WE,
  input  [7:0] entre,
  output [7:0] sortie
);

  wire clock_1_out;

  Clock clock_1 (.out(clock_1_out));
  RAM ram_1 (.addr(adresse), .we(WE), .oe(1'b1), .clk(clock_1_out), .din(entre), .dout(sortie));
endmodule

module ProgramCounter (
  input  [7:0] instruction,
  output [7:0] out_2
);

  wire clock_1_out;

  Register register_1 (.D(instruction), .en(1'b1), .clk(clock_1_out), .Q(out_2));  // open: clr
  Clock clock_1 (.out(clock_1_out));
endmodule

module extendPC (
  input  [7:0] ADDR8,
  input  JUMP,
  input  init,
  output [7:0] out_4
);

  wire [7:0] adder_1_out, multiplexer_1_out, programcounter_1_out_2;

  ProgramCounter programcounter_1 (.instruction(out_4), .out_2(programcounter_1_out_2));
  Adder adder_1 (.a(programcounter_1_out_2), .b(8'h1), .out(adder_1_out));  // open: cin, cout
  Multiplexer #(.width(8)) multiplexer_1 (.in0(adder_1_out), .in1({8{1'b0}}), .out(multiplexer_1_out), .sel(init));
  Multiplexer #(.width(8)) multiplexer_2 (.in0(multiplexer_1_out), .in1(ADDR8), .out(out_4), .sel(JUMP));
endmodule

module FETCH (
  input  [23:0] instruction,
  output [23:0] out_2
);

  wire clock_1_out;

  Register #(.width(24)) register_1 (.D(instruction), .en(1'b1), .clk(clock_1_out), .Q(out_2));  // open: clr
  Clock clock_1 (.out(clock_1_out));
endmodule

module CheminDonnees (
  input  [7:0] ADDR8,
  input  JUMP,
  input  init,
  output [23:0] out_4
);

  wire [7:0] extendpc_1_out_4;
  wire [23:0] fetch_1_out_2, raminstructions_1_sortie;

  extendPC extendpc_1 (.ADDR8(ADDR8), .JUMP(JUMP), .init(init), .out_4(extendpc_1_out_4));
  RAMinstructions raminstructions_1 (.adresse(extendpc_1_out_4), .init(init), .sortie(raminstructions_1_sortie));
  FETCH fetch_1 (.instruction(raminstructions_1_sortie), .out_2(fetch_1_out_2));
  Multiplexer #(.width(24)) multiplexer_1 (.in0(fetch_1_out_2), .in1({24{1'b0}}), .out(out_4), .sel(JUMP));
endmodule

module addressingRegisters (
  input  [7:0] ALU,
  input  [7:0] RAM,
  input  [7:0] CNST8,
  input  [1:0] instruction,
  output [7:0] REG_IN
);

  Multiplexer #(.select(2), .width(8)) multiplexer_1 (
    .in0(ALU), .in1(RAM), .in2(CNST8), .out(REG_IN), .sel(instruction));  // open: in3
endmodule
